// Logisim project finishing of game simulation.circ as structural Verilog: 1 circuit, main circuit main
module main (
  input  Default_1,
  output out_2,
  output out_3,
  output out_4,
  output out_5,
  output out_6,
  output out_7,
  output out_8,
  output out_9,
  output out_10,
  output out_11,
  output out_12,
  output out_13
);

  wire Clockpulse_Genaretor_out, decoder_1_out0, decoder_1_out1, decoder_1_out2, decoder_1_out3,
       decoder_1_out4, decoder_1_out5, decoder_1_out6, decoder_1_out7, decoder_1_out8, decoder_1_out9,
       decoder_1_out10, decoder_1_out11, decoder_1_out12, decoder_1_out13, decoder_1_out14, decoder_1_out15,
       decoder_2_out0, decoder_2_out1, decoder_2_out2, decoder_2_out3, decoder_2_out4, decoder_2_out5,
       decoder_2_out6, decoder_3_out0, decoder_3_out1, decoder_3_out2, decoder_3_out3, decoder_3_out4,
       decoder_3_out5, decoder_3_out6, decoder_4_out0, decoder_4_out1, decoder_4_out2, decoder_4_out3,
       decoder_4_out4, decoder_4_out5, decoder_4_out6, decoder_4_out7, j_k_ff_1_qn, j_k_ff_2_qn, j_k_ff_3_qn,
       j_k_ff_5_qn, j_k_ff_6_qn, j_k_ff_7_qn, j_k_ff_9_qn, j_k_ff_10_qn, j_k_ff_11_qn, nand_1_out,
       nand_2_out, not_1_out, or_1_out, or_2_out, or_3_out, or_4_out, priority_encoder_1_gs,
       priority_encoder_2_gs, priority_encoder_3_gs, Shoot_Hit_out, Start_out;
  wire [3:0] priority_encoder_1_out, priority_encoder_2_out, priority_encoder_3_out, subtractor_1_out;

  not not_1 (not_1_out, Clockpulse_Genaretor_out);
  J_K_Flip_Flop j_k_ff_1 (
    .J(Default_1), .clk(not_1_out), .K(Default_1), .Q(out_3), .Qn(j_k_ff_1_qn), .reset(or_1_out));  // open: preset, en
  J_K_Flip_Flop j_k_ff_2 (
    .J(Default_1), .clk(j_k_ff_1_qn), .K(Default_1), .Q(out_5), .Qn(j_k_ff_2_qn), .reset(or_1_out));  // open: preset, en
  J_K_Flip_Flop j_k_ff_3 (
    .J(Default_1), .clk(j_k_ff_2_qn), .K(Default_1), .Q(out_7), .Qn(j_k_ff_3_qn), .reset(or_1_out));  // open: preset, en
  J_K_Flip_Flop j_k_ff_4 (
    .J(Default_1), .clk(j_k_ff_3_qn), .K(Default_1), .Q(out_9), .reset(or_1_out));  // open: Qn, preset, en
  Button Start (.out(Start_out));
  or or_1 (or_1_out, or_4_out, Start_out);
  Clock Clockpulse_Genaretor (.out(Clockpulse_Genaretor_out));
  Decoder #(.select(4)) decoder_1 (
    .out0(decoder_1_out0), .out1(decoder_1_out1), .out2(decoder_1_out2), .out3(decoder_1_out3),
    .out4(decoder_1_out4), .out5(decoder_1_out5), .out6(decoder_1_out6), .out7(decoder_1_out7),
    .out8(decoder_1_out8), .out9(decoder_1_out9), .out10(decoder_1_out10), .out11(decoder_1_out11),
    .out12(decoder_1_out12), .out13(decoder_1_out13), .out14(decoder_1_out14), .out15(decoder_1_out15),
    .sel({out_9, out_7, out_5, out_3}));  // open: en
  Button Shoot_Hit (.out(Shoot_Hit_out));
  LED E (.in(decoder_1_out0));
  LED E_2 (.in(decoder_1_out1));
  LED led_1 (.in(decoder_1_out2));
  LED led_2 (.in(decoder_1_out3));
  LED E_3 (.in(decoder_1_out4));
  LED led_3 (.in(decoder_1_out5));
  LED led_4 (.in(decoder_1_out6));
  LED led_5 (.in(decoder_1_out7));
  LED E_4 (.in(decoder_1_out8));
  LED led_6 (.in(decoder_1_out9));
  LED led_7 (.in(decoder_1_out9));
  LED led_8 (.in(decoder_1_out10));
  LED led_9 (.in(decoder_1_out11));
  LED E_5 (.in(decoder_1_out12));
  LED led_10 (.in(decoder_1_out13));
  LED led_11 (.in(decoder_1_out14));
  LED led_12 (.in(decoder_1_out15));
  or or_2 (or_2_out, decoder_1_out0, decoder_1_out4, decoder_1_out1, decoder_1_out8, decoder_1_out12);
  or or_3 (or_3_out, decoder_1_out2, decoder_1_out3, decoder_1_out5, decoder_1_out6, decoder_1_out7, decoder_1_out9, decoder_1_out10, decoder_1_out11, decoder_1_out13, decoder_1_out14, decoder_1_out15);
  or or_4 (or_4_out, decoder_2_out6, decoder_3_out6);
  nand nand_1 (nand_1_out, or_2_out, Shoot_Hit_out);
  // AND_Gate and_1 has open pins: in0=or_2_out, in1=Shoot_Hit_out, out=open
  nand nand_2 (nand_2_out, or_3_out, Shoot_Hit_out);
  J_K_Flip_Flop j_k_ff_5 (
    .J(Default_1), .clk(nand_1_out), .K(Default_1), .Q(out_2), .Qn(j_k_ff_5_qn), .reset(or_1_out));  // open: preset, en
  J_K_Flip_Flop j_k_ff_6 (
    .J(Default_1), .clk(j_k_ff_5_qn), .K(Default_1), .Q(out_4), .Qn(j_k_ff_6_qn), .reset(or_1_out));  // open: preset, en
  J_K_Flip_Flop j_k_ff_7 (
    .J(Default_1), .clk(j_k_ff_6_qn), .K(Default_1), .Q(out_6), .Qn(j_k_ff_7_qn), .reset(or_1_out));  // open: preset, en
  J_K_Flip_Flop j_k_ff_8 (
    .J(Default_1), .clk(j_k_ff_7_qn), .K(Default_1), .Q(out_8), .reset(or_1_out));  // open: Qn, preset, en
  J_K_Flip_Flop j_k_ff_9 (
    .J(Default_1), .clk(nand_2_out), .K(Default_1), .Q(out_10), .Qn(j_k_ff_9_qn), .reset(or_1_out));  // open: preset, en
  J_K_Flip_Flop j_k_ff_10 (
    .J(Default_1), .clk(j_k_ff_9_qn), .K(Default_1), .Q(out_11), .Qn(j_k_ff_10_qn), .reset(or_1_out));  // open: preset, en
  J_K_Flip_Flop j_k_ff_11 (
    .J(Default_1), .clk(j_k_ff_10_qn), .K(Default_1), .Q(out_12), .Qn(j_k_ff_11_qn), .reset(or_1_out));  // open: preset, en
  J_K_Flip_Flop j_k_ff_12 (
    .J(Default_1), .clk(j_k_ff_11_qn), .K(Default_1), .Q(out_13), .reset(or_1_out));  // open: Qn, preset, en
  Decoder #(.select(4)) decoder_2 (
    .out0(decoder_2_out0), .out1(decoder_2_out1), .out2(decoder_2_out2), .out3(decoder_2_out3),
    .out4(decoder_2_out4), .out5(decoder_2_out5), .out6(decoder_2_out6), .sel({out_8, out_6, out_4, out_2}));  // open: out7, out8, out9, out10, out11, out12, out13, out14, out15, en
  Subtractor #(.width(4)) subtractor_1 (
    .a({out_8, out_6, out_4, out_2}), .b({out_13, out_12, out_11, out_10}), .out(subtractor_1_out));  // open: bin, bout
  Decoder #(.select(4)) decoder_3 (
    .out0(decoder_3_out0), .out1(decoder_3_out1), .out2(decoder_3_out2), .out3(decoder_3_out3),
    .out4(decoder_3_out4), .out5(decoder_3_out5), .out6(decoder_3_out6),
    .sel({out_13, out_12, out_11, out_10}));  // open: out7, out8, out9, out10, out11, out12, out13, out14, out15, en
  Hex_Digit_Display hex_digit_display_1 (.value(priority_encoder_1_out), .dp(priority_encoder_1_gs));
  Priority_Encoder #(.select(4)) priority_encoder_1 (
    .in0(decoder_2_out0), .in1(decoder_2_out1), .in2(decoder_2_out2), .in3(decoder_2_out3),
    .in4(decoder_2_out4), .in5(decoder_2_out5), .out(priority_encoder_1_out), .gs(priority_encoder_1_gs));  // open: in6, in7, in8, in9, in10, in11, in12, in13, in14, in15, en_out, en_in
  Decoder #(.select(4)) decoder_4 (
    .out0(decoder_4_out0), .out1(decoder_4_out1), .out2(decoder_4_out2), .out3(decoder_4_out3),
    .out4(decoder_4_out4), .out5(decoder_4_out5), .out6(decoder_4_out6), .out7(decoder_4_out7),
    .sel(subtractor_1_out));  // open: out8, out9, out10, out11, out12, out13, out14, out15, en
  Priority_Encoder #(.select(4)) priority_encoder_2 (
    .in0(decoder_3_out0), .in1(decoder_3_out1), .in2(decoder_3_out2), .in3(decoder_3_out3),
    .in4(decoder_3_out4), .in5(decoder_3_out5), .out(priority_encoder_2_out), .gs(priority_encoder_2_gs));  // open: in6, in7, in8, in9, in10, in11, in12, in13, in14, in15, en_out, en_in
  Hex_Digit_Display hex_digit_display_2 (.value(priority_encoder_3_out), .dp(priority_encoder_3_gs));
  Priority_Encoder #(.select(4)) priority_encoder_3 (
    .in0(decoder_4_out0), .in1(decoder_4_out1), .in2(decoder_4_out2), .in3(decoder_4_out3),
    .in4(decoder_4_out4), .in5(decoder_4_out5), .in6(decoder_4_out6), .in7(decoder_4_out7),
    .out(priority_encoder_3_out), .gs(priority_encoder_3_gs));  // open: in8, in9, in10, in11, in12, in13, in14, in15, en_out, en_in
  Hex_Digit_Display hex_digit_display_3 (.value(priority_encoder_2_out), .dp(priority_encoder_2_gs));

  // Notes on the sheet:
  //   Number of hitting correct= true -false
  //   Number of hitting true value
  //   Number of hitting false value
endmodule
